# Fritzing sketch led (saved by Fritzing 0.9.4)
breadboards: 1

parts:
  LED1 = smd LED [color="Red (633nm)" package="1206 [SMD]"]
  R1 = Resistor [tolerance=±5% resistance=220 package="2512 [SMD]"]
  Raspberry_Pi_1 = Raspberry Pi 3 [part_number=RPI-3-V1.2]

nets:
  N1: LED1.cathode, Raspberry_Pi_1.GND
  N2: LED1.anode, R1.Pin_0
  N3: R1.Pin_1, Raspberry_Pi_1.GIPO23
