# Fritzing sketch servo (saved by Fritzing 0.9.4)

parts:
  Raspberry_Pi_1 = Raspberry Pi 3 [part_number=RPI-3-V1.2]
  J1 = Basic Servo
  VCC1 = 4 x AAA Battery Mount

nets:
  GND: Raspberry_Pi_1.GND, J1.gnd, VCC1.-
  N1: Raspberry_Pi_1.GIPO23, J1.pulse
  N2: J1.vcc, VCC1.+
